# Fritzing sketch all (saved by Fritzing 0.9.3b)
breadboards: 2

parts:
  Part1 = Arduino Uno (Rev3)
  LED3 = smd LED [color="Infrared (850nm)" package="0805 [SMD]"]
  R2 = Resistor [tolerance=±5% resistance=330 package=THT]
  R1 = Resistor [tolerance=±5% resistance=330 package=THT]
  R3 = Resistor [tolerance=±5% resistance=10k package=THT]
  LED4 = smd LED [color="Red (633nm)" package="0805 [SMD]"]
  J2 = Piezo Speaker
  R4 = Resistor [tolerance=±5% resistance=220 package="1206 [SMD]"]
  LED2 = smd LED [color="Infrared (940nm)" package="0805 [SMD]"]
  Raspberry_Pi_2 = Raspberry Pi 3 [part_number=RPI-3-V1.2]

nets:
  N1: Part1.A0, R3.Pin_0, LED2.anode
  N2: Part1.D8, R3.Pin_1
  N3: Part1.GND, LED3.cathode, LED2.cathode
  N4: Part1.5V, R2.Pin_0, R1.Pin_0
  N5: LED3.anode, R2.Pin_1, R1.Pin_1
  N6: LED4.cathode, J2.pin1, Raspberry_Pi_2.GND
  N7: LED4.anode, R4.Pin_1
  N8: J2.pin2, Raspberry_Pi_2.GIPO23
  N9: R4.Pin_0, Raspberry_Pi_2.GIPO18
