# Fritzing sketch raspberry_pi (saved by Fritzing 0.9.3b)
breadboards: 1

parts:
  Raspberry_Pi_1 = Raspberry Pi 3 [part_number=RPI-3-V1.2]
  LED1 = smd LED [color="Red (633nm)" package="0805 [SMD]"]
  J1 = Piezo Speaker
  R1 = Resistor [tolerance=±5% resistance=220 package="1206 [SMD]"]

nets:
  N1: Raspberry_Pi_1.GIPO23, J1.pin2
  N2: Raspberry_Pi_1.GIPO18, R1.Pin_1
  N3: Raspberry_Pi_1.GND, LED1.cathode, J1.pin1
  N4: LED1.anode, R1.Pin_0
