# Fritzing sketch sketch (saved by Fritzing 0.9.3b)
breadboards: 1

parts:
  Part1 = Arduino Uno (Rev3)
  LED1 = smd LED [color="Red (633nm)" package="0603 [SMD]"]
  LED3 = smd LED [color="Infrared (850nm)" package="0805 [SMD]"]
  LED2 = smd LED [color="Infrared (940nm)" package="0805 [SMD]"]
  R2 = Resistor [tolerance=±5% resistance=330 package=THT]
  R1 = Resistor [tolerance=±5% resistance=220 package=THT]
  R1_2 = Resistor [tolerance=±5% resistance=330 package=THT]
  R3 = Resistor [tolerance=±5% resistance=10k package=THT]
  J1 = Piezo Speaker
  R4 = Resistor [tolerance=±5% resistance=330 package=THT]

nets:
  N1: Part1.A0, LED2.anode, R3.Pin_0
  N2: Part1.D8, R3.Pin_1
  N3: Part1.D9_PWM, J1.pin2
  N4: Part1.D10_PWM/SS, R4.Pin_1
  N5: Part1.GND, LED1.cathode, LED3.cathode, LED2.cathode, J1.pin1
  N6: Part1.5V, R2.Pin_1, R1.Pin_1, R1_2.Pin_1
  N7: LED1.anode, R4.Pin_0
  N8: LED3.anode, R2.Pin_0, R1.Pin_0, R1_2.Pin_0
